# Fritzing sketch Sketch (saved by Fritzing 0.9.3b)
breadboards: 1

parts:
  Arduino = Arduino Uno (Rev3)
  20x4_LCD = LCD screen
  R1 = Resistor [tolerance=±5% resistance=10 package=THT]
  R2 = Resistor [tolerance=±5% resistance=330 package=THT]
  Up_Button = Pushbutton [package="[THT]"]
  Down_Button = Pushbutton [package="[THT]"]
  R3 = Resistor [tolerance=±5% resistance=1k package=THT]
  R4 = Resistor [tolerance=±5% resistance=1k package=THT]

nets:
  N1: Arduino.D8, 20x4_LCD.RS
  N2: Arduino.D10_PWM/SS, Up_Button.Pin_1, Up_Button.Pin_2, R3.Pin_1
  N3: Arduino.D11_PWM/MOSI, Down_Button.Pin_1, Down_Button.Pin_2, R4.Pin_1
  GND: Arduino.GND, 20x4_LCD.VSS, 20x4_LCD.R/W, 20x4_LCD.LED-, R2.Pin_0, R3.Pin_0, R4.Pin_0
  N4: Arduino.D2, 20x4_LCD.DB7
  N5: Arduino.D3_PWM, 20x4_LCD.DB6
  N6: Arduino.D4, 20x4_LCD.DB5
  N7: Arduino.D5_PWM, 20x4_LCD.DB4
  N8: Arduino.D6_PWM, 20x4_LCD.E
  5V: Arduino.5V, 20x4_LCD.VDD, R1.Pin_0, Up_Button.Pin_3, Up_Button.Pin_4, Down_Button.Pin_3, Down_Button.Pin_4
  N9: 20x4_LCD.V0, R2.Pin_1
  N10: 20x4_LCD.LED+, R1.Pin_1

notes:
  Note 1) R3 and R4 can be any resistor between 1K to 2K.
  Note 2) You man need a different resistor for R2. It's connected to LCD contrast adjustment (purple wire). Each LCD works best with different value. You can use a potensiometer there and adjust that.
  Note 3) You can remove the R1, depending on your LCD. Try different resistors there to find the best value for your LCD, or use a potensiometer.
